# Fritzing sketch Programmer Connection (saved by Fritzing 0.9.3b)
breadboards: 1

parts:
  PIC_16F877A1 = PIC 16F877A [package=THT]
  Y1 = CRYSTAL [package=hc49us]
  JP2 = Header 6 [package=molex-1x6_lock]  # not connected
  R1 = Resistor [tolerance=±5% resistance=10k package=THT]

nets:
  N1: PIC_16F877A1.RA0/AN0, R1.Pin_0
  N2: PIC_16F877A1.VSS#11, R1.Pin_1
  N3: PIC_16F877A1.OSC2/CLKOUT, Y1.2
  N4: PIC_16F877A1.RC0, Y1.1

notes:
  +5 V
  0 V
  1
  20
  21
  40
  13
  14
  12
  11
  33
  2
  3
  4
  5
  39
  10 k Ohm
  Programmer Pins
