# Fritzing sketch Untitled Sketch (saved by Fritzing 0.9.3b)
breadboards: 1

parts:
  PIC_16F877A1 = PIC 16F877A [package=THT]
  Y1 = CRYSTAL [package=hc49us]
  R1 = Resistor [tolerance=±5% resistance=220 package="2512 [SMD]"]
  LED1 = smd LED [color="Red (633nm)" package="1206 [SMD]"]

nets:
  N1: PIC_16F877A1.RA0/AN0, PIC_16F877A1.VSS#11
  N2: PIC_16F877A1.OSC1/CLKIN, LED1.cathode
  N3: PIC_16F877A1.OSC2/CLKOUT, Y1.2
  N4: PIC_16F877A1.RC0, Y1.1
  N5: PIC_16F877A1.VDD#31, R1.Pin_1
  N6: R1.Pin_0, LED1.anode

notes:
  +5 V
  0 V
  1
  20
  21
  40
  13
  14
  12
  11
  33
  +ve
  -ve
