# Fritzing sketch Timer Interrupt (saved by Fritzing 0.9.3b)
breadboards: 1

parts:
  PIC_16F877A1 = PIC 16F877A [package=THT]
  Y1 = CRYSTAL [package=hc49us]
  U1 = LCD-16X2 [package=lcd-16x2_noholes]
  R1 = Resistor [tolerance=±5% resistance=220 package="0402 [SMD]"]
  PIC_16F877A2 = PIC 16F877A [package=THT]

nets:
  N1: PIC_16F877A1.MCLR, PIC_16F877A1.VDD#10, PIC_16F877A2.MCLR, PIC_16F877A2.VDD#10
  N2: PIC_16F877A1.RA0/AN0, PIC_16F877A2.RA0/AN0
  N3: PIC_16F877A1.RA1/AN1, PIC_16F877A2.RA1/AN1
  N4: PIC_16F877A1.RA2/AN2, PIC_16F877A2.RA2/AN2
  N5: PIC_16F877A1.RA3/AN3, PIC_16F877A2.RA3/AN3
  N6: PIC_16F877A1.RA4, PIC_16F877A2.RA4
  N7: PIC_16F877A1.RA5/AN4/SS, PIC_16F877A2.RA5/AN4/SS
  N8: PIC_16F877A1.RE0/RD/AN5, PIC_16F877A2.RE0/RD/AN5
  N9: PIC_16F877A1.RE1/WR/AN6, PIC_16F877A2.RE1/WR/AN6
  N10: PIC_16F877A1.RE2/CS/AN7, PIC_16F877A2.RE2/CS/AN7
  N11: PIC_16F877A1.VSS#11, PIC_16F877A2.VSS#11
  N12: PIC_16F877A1.OSC1/CLKIN, Y1.2, PIC_16F877A2.OSC1/CLKIN
  N13: PIC_16F877A1.OSC2/CLKOUT, Y1.1, PIC_16F877A2.OSC2/CLKOUT
  N14: PIC_16F877A1.RC0, PIC_16F877A2.RC0
  N15: PIC_16F877A1.RC1, PIC_16F877A2.RC1
  N16: PIC_16F877A1.RC2, PIC_16F877A2.RC2
  N17: PIC_16F877A1.RC3, PIC_16F877A2.RC3
  N18: PIC_16F877A1.RD0/PSP0, PIC_16F877A2.RD0/PSP0
  N19: PIC_16F877A1.RD1/PSP1, PIC_16F877A2.RD1/PSP1
  N20: PIC_16F877A1.RD2/PSP2, PIC_16F877A2.RD2/PSP2
  N21: PIC_16F877A1.RD3/PSP3, PIC_16F877A2.RD3/PSP3
  N22: PIC_16F877A1.RC4, PIC_16F877A2.RC4
  N23: PIC_16F877A1.RC5, PIC_16F877A2.RC5
  N24: PIC_16F877A1.RC6/TX/CK, PIC_16F877A2.RC6/TX/CK
  N25: PIC_16F877A1.RC7/RX/DT, PIC_16F877A2.RC7/RX/DT
  N26: PIC_16F877A1.RD4/PSP4, PIC_16F877A2.RD4/PSP4
  N27: PIC_16F877A1.RD5/PSP5, PIC_16F877A2.RD5/PSP5
  N28: PIC_16F877A1.RD6/PSP6, PIC_16F877A2.RD6/PSP6
  N29: PIC_16F877A1.RD7/PSP7, PIC_16F877A2.RD7/PSP7
  VSS: PIC_16F877A1.VSS#30, PIC_16F877A1.VDD#31, U1.VSS, U1.VDD, U1.A, U1.K, R1.Pin_1, PIC_16F877A2.VSS#30, PIC_16F877A2.VDD#31
  N30: PIC_16F877A1.RB0/INT, PIC_16F877A2.RB0/INT
  N31: PIC_16F877A1.RB1, U1.DB5, PIC_16F877A2.RB1
  N32: PIC_16F877A1.RB2, PIC_16F877A2.RB2
  N33: PIC_16F877A1.RB3, PIC_16F877A2.RB3
  N34: PIC_16F877A1.RB4, PIC_16F877A2.RB4
  N35: PIC_16F877A1.RB5, U1.VO, R1.Pin_0, PIC_16F877A2.RB5
  N36: PIC_16F877A1.RB6, PIC_16F877A2.RB6
  N37: PIC_16F877A1.RB7, PIC_16F877A2.RB7

notes:
  +5 V
  0 V
  1
  20
  21
  40
  13
  14
  12
  11
  33
  19
  32
  31
  k
  A
  D7
  D6
  D5
  v0
  vDD
  vss
  Rs
  Rw
  E
